# Fritzing sketch Tableau de bord (saved by Fritzing 0.9.3b)
circuit board: 8.46667cm x 5.64444cm
perfboards: 1

parts:
  N2 = LED - 3mm [color="Orange (620nm)" package="3 mm [THT]"]
  N3 = LED - 3mm [color="Blue (430nm)" package="3 mm [THT]"]
  J1 = Screw terminal - 2 pins [package=THT]
  J2 = Screw terminal - 2 pins [package=THT]
  J3 = Screw terminal - 2 pins [package=THT]
  J5 = Screw terminal - 2 pins [package=THT]
  R3 = Resistor [tolerance=±5% resistance=220 package=THT]
  J6 = Screw terminal - 2 pins [package=THT]
  R4 = Resistor [tolerance=±5% resistance=310 package=THT]
  J4 = Screw terminal - 2 pins [package=THT]
  J7 = Screw terminal - 2 pins [package=THT]
  N4 = LED - 3mm [color="Green (555nm)" package="3 mm [THT]"]
  R5 = Resistor [tolerance=±5% resistance=220 package=THT]
  R6 = Resistor [tolerance=±5% resistance=220 package=THT]
  R7 = Resistor [tolerance=±5% resistance=220 package=THT]

nets:
  N1: N2.cathode, R3.Pin_1
  N2: N2.anode, N3.anode, J6.pin2, J4.pin2, J7.pin1
  N3: N3.cathode, R4.Pin_0
  N4: J1.pin1, R4.Pin_1, N4.anode, R7.Pin_0
  N5: J1.pin2, J4.pin1, R6.Pin_0
  N6: J2.pin1, J5.pin2
  N7: J2.pin2, J5.pin1
  N8: J3.pin1, R5.Pin_1
  N9: J3.pin2, R3.Pin_0
  N10: J6.pin1, R7.Pin_1
  N11: J7.pin2, R6.Pin_1
  N12: N4.cathode, R5.Pin_0

notes:
  +5V
  GND
  R_IN
  L_IN
  HB (+7V)
  N (GND)
  TURN
  R_OUT
  L_OUT
  INSTR+
